# Fritzing sketch Kamstrup602 (saved by Fritzing 0.9.0b)
breadboards: 1

parts:
  Part1 = Arduino Uno (Rev3)
  R1 = Resistor [tolerance=±5% resistance=10k package=THT]
  R2 = Resistor [tolerance=±5% resistance=22k package=THT]
  R3 = Resistor [tolerance=±5% resistance=22k package=THT]

nets:
  N1: Part1.D9_PWM, R1.Pin_1
  N2: Part1.D10_PWM/SS, R2.Pin_0, R3.Pin_0
  N3: Part1.5V, R1.Pin_0
  N4: R2.Pin_1, R3.Pin_1
